# Fritzing sketch 8266OLED_I2C (saved by Fritzing 0.9.3b)
breadboards: 1

parts:
  U1 = NodeMCU V1.0
  Squix1 = OLED 0.96" 128x64 I2C SSD1306

nets:
  N1: U1.D3, Squix1.SCA
  3V3: U1.3V3, Squix1.VCC
  GND: U1.GND, Squix1.GND
  N2: U1.D5, Squix1.SCL

custom parts:
  NodeMCU V1.0: ESP8266 based NodeMCU
